// Logisim project schema1.circ as structural Verilog: 1 circuit, main circuit main
module main (
  input  in_1,
  input  in_2,
  input  in_3,
  input  in_4
);

  wire Alu2_GT_Alu1, Alu_1_In, Alu_2_In, Alu_Op_H, Alu_Op_L, Alu_Out, and_1_out, and_2_out, button_1_out,
       button_2_out, Carry_In, Carry_out, clock, clock_1_out, decoder_1_out0, decoder_1_out1, decoder_1_out2,
       decoder_1_out3, decoder_2_out0, decoder_2_out1, decoder_2_out2, decoder_2_out3, demultiplexer_1_out0,
       demultiplexer_1_out1, Flag_zero, Halt, Instruction_Register_Enable, IP_Advance, Memory_In,
       Memory_Input_Select, Memory_out, Micro_Reset, or_1_out, Register_In_Enable, Register_In_H,
       Register_In_L, Register_Out_Enable, Register_Out_H, Register_Out_L, Reset, Write_Memory_Enable,
       Write_Memory_Select, Zero_Out;
  wire [7:0] A_q, adder_1_out, ALU1_q, ALU2_q, B_q, C_q, D_q, Instruction, Micro_Counter, multiplexer_2_out,
       nand_1_out, ram_1_data, subtractor_1_out, xor_1_out;
  wire [15:0] IP_q, Low_q, multiplexer_1_out;
  wire [23:0] rom_1_data;

  or or_1 (or_1_out, Micro_Reset, Reset);
  Demultiplexer #(.enable("false")) demultiplexer_1 (
    .out0(demultiplexer_1_out0), .out1(demultiplexer_1_out1), .in(Write_Memory_Enable),
    .sel(Write_Memory_Select));
  Multiplexer #(.width(16), .enable("false")) multiplexer_1 (
    .in0(IP_q), .in1(Low_q), .out(multiplexer_1_out), .sel(Memory_Input_Select));
  and and_1 (and_1_out, Halt, button_1_out);
  Button button_1 (.out(button_1_out));
  and and_2 (and_2_out, ~Halt, clock_1_out);  // AND_Gate
  Clock clock_1 (.out(clock_1_out));
  Counter counter_1 (.count(1'b1), .Q(Micro_Counter), .clk(clock), .clr(or_1_out));  // open: load, D, carry
  Counter #(.width(16), .max('hffff)) IP (
    .count(1'b1), .Q(IP_q), .clk(IP_Advance), .clr(Reset));  // open: load, D, carry
  Register High (.D(ram_1_data), .en(demultiplexer_1_out1), .Q(Low_q[15:8]), .clk(clock), .clr(Reset));
  or or_2 (clock, and_1_out, and_2_out);
  Register Low (.D(ram_1_data), .en(demultiplexer_1_out0), .Q(Low_q[7:0]), .clk(clock), .clr(Reset));
  RAM #(.addrWidth(16), .bus("separate")) ram_1 (
    .addr(multiplexer_1_out), .din(ram_1_data), .data(ram_1_data), .str(Memory_In), .clk(clock),
    .ld(Memory_out));  // open: sel, clr
  assign ram_1_data = Zero_Out ? {8{1'b0}} : 8'bz;  // Controlled_Buffer controlled_buffer_1
  // Probe on ram_1_data
  Register ALU1 (.D(ram_1_data), .en(Alu_1_In), .Q(ALU1_q), .clk(clock), .clr(Reset));
  Register ALU2 (.D(ram_1_data), .en(Alu_2_In), .Q(ALU2_q), .clk(clock), .clr(Reset));
  Register A (.D(ram_1_data), .en(decoder_2_out0), .Q(A_q), .clk(clock), .clr(Reset));
  assign ram_1_data = decoder_1_out0 ? A_q : 8'bz;  // Controlled_Buffer controlled_buffer_2
  assign ram_1_data = decoder_1_out1 ? B_q : 8'bz;  // Controlled_Buffer controlled_buffer_3
  Register B (.D(ram_1_data), .en(decoder_2_out1), .Q(B_q), .clk(clock), .clr(Reset));
  assign ram_1_data = decoder_1_out2 ? C_q : 8'bz;  // Controlled_Buffer controlled_buffer_4
  Register C (.D(ram_1_data), .en(decoder_2_out2), .Q(C_q), .clk(clock), .clr(Reset));
  Register D (.D(ram_1_data), .en(decoder_2_out3), .Q(D_q), .clk(clock), .clr(Reset));
  assign ram_1_data = decoder_1_out3 ? D_q : 8'bz;  // Controlled_Buffer controlled_buffer_5
  Adder adder_1 (.a(ALU1_q), .b(ALU2_q), .out(adder_1_out), .cin(Carry_In), .cout(Carry_out));
  Subtractor subtractor_1 (.a(ALU1_q), .b(ALU2_q), .out(subtractor_1_out), .bin(Carry_In), .bout(Alu2_GT_Alu1));
  assign nand_1_out = ~(ALU1_q & ALU2_q);  // NAND_Gate nand_1, 8 bits wide
  assign xor_1_out = ALU1_q ^ ALU2_q;  // XOR_Gate xor_1, 8 bits wide
  Decoder #(.select(2), .disabled(0)) decoder_1 (
    .out0(decoder_1_out0), .out1(decoder_1_out1), .out2(decoder_1_out2), .out3(decoder_1_out3),
    .sel({Register_Out_H, Register_Out_L}), .en(Register_Out_Enable));
  Decoder #(.select(2), .disabled(0)) decoder_2 (
    .out0(decoder_2_out0), .out1(decoder_2_out1), .out2(decoder_2_out2), .out3(decoder_2_out3),
    .sel({Register_In_H, Register_In_L}), .en(Register_In_Enable));
  Register register_1 (.D(ram_1_data), .en(Instruction_Register_Enable), .Q(Instruction), .clk(clock), .clr(Reset));
  assign ram_1_data = Alu_Out ? multiplexer_2_out : 8'bz;  // Controlled_Buffer controlled_buffer_6
  nand nand_2 (Flag_zero, multiplexer_2_out[0], multiplexer_2_out[1], multiplexer_2_out[2], multiplexer_2_out[3], multiplexer_2_out[4], multiplexer_2_out[5], multiplexer_2_out[6], multiplexer_2_out[7]);
  Multiplexer #(.select(2), .width(8), .enable("false")) multiplexer_2 (
    .in0(adder_1_out), .in1(subtractor_1_out), .in2(nand_1_out), .in3(xor_1_out), .out(multiplexer_2_out),
    .sel({Alu_Op_H, Alu_Op_L}));
  Button button_2 (.out(button_2_out));
  or or_3 (Reset, button_2_out, rom_1_data[0]);
  ROM #(.addrWidth(16), .dataWidth(24)) rom_1 (
    .addr({Instruction, Micro_Counter}),
    .data({rom_1_data[23], Zero_Out, Alu_Out, Alu_Op_H, Alu_Op_L, Carry_In, Alu_2_In, Alu_1_In, Instruction_Register_Enable, Memory_out, IP_Advance, Memory_Input_Select, Write_Memory_Select, Write_Memory_Enable, Memory_In, Halt, Register_In_H, Register_In_L, Register_In_Enable, Register_Out_H, Register_Out_L, Register_Out_Enable, Micro_Reset, rom_1_data[0]}));  // open: sel

  // Notes on the sheet:
  //   contents of rom_1 (hex, n*v repeats v):
  //   c000 2000 0 24 252*2 c000 2000 0 2c 252*2 c000 2000 0 34 252*2 c000 2000 0 3c 252*2 c000 2000 0 64
  //   252*2 c000 2000 0 6c 252*2 c000 2000 0 74 252*2 c000 2000 0 7c 252*2 c000 2000 0 a4 252*2 c000 2000
  //   0 ac 252*2 c000 2000 0 b4 252*2 c000 2000 0 bc 252*2 c000 2000 0 e4 252*2 c000 2000 0 ec 252*2 c000
  //   2000 0 f4 252*2 c000 2000 0 fc 252*2 c000 2000 0 5020 252*2 c000 2000 0 5060 252*2 c000 2000 0 50a0
  //   252*2 c000 2000 0 50e0 252*2 c000 2000 0 1204 252*2 c000 2000 0 120c 252*2 c000 2000 0 1214 252*2
  //   c000 2000 0 121c 252*2 c000 2000 0 1404 252*2 c000 2000 0 140c 252*2 c000 2000 0 1414 252*2 c000
  //   2000 0 141c 252*2 c000 2000 0 1c04 252*2 c000 2000 0 1c0c 252*2 c000 2000 0 1c14 252*2 c000 2000 0
  //   1c1c 252*2 c000 2000 0 4020 2000 251*2 c000 2000 0 4060 2000 251*2 c000 2000 0 40a0 2000 251*2 c000
  //   2000 0 40e0 2000 251*2 c000 2000 0 253*2 c000 2000 0 253*2 c000 2000 0 253*2 c000 2000 0 253*2 c000
  //   2000 0 253*2 c000 2000 0 253*2 c000 2000 0 253*2 c000 2000 0 253*2 c000 2000 0 253*2 c000 2000 0
  //   253*2 c000 2000 0 253*2 c000 2000 0 253*2 c000 2000 0 253*2 c000 2000 0 253*2 c000 2000 0 253*2 c000
  //   2000 0 253*2 c000 2000 0 253*2 c000 2000 0 253*2 c000 2000 0 253*2 c000 2000 0 253*2 c000 2000 0
  //   253*2 c000 2000 0 253*2 c000 2000 0 253*2 c000 2000 0 253*2 c000 2000 0 253*2 c000 2000 0 253*2 c000
  //   2000 0 253*2 c000 2000 0 253*2 c000 2000 0 253*2 c000 2000 0 253*2 c000 2000 0 253*2 c000 2000 0
  //   253*2 c000 2000 0 253*2 c000 2000 0 253*2 c000 2000 0 253*2 c000 2000 0 253*2 c000 2000 0 253*2 c000
  //   2000 0 253*2 c000 2000 0 253*2 c000 2000 0 253*2 c000 2000 0 253*2 c000 2000 0 253*2 c000 2000 0
  //   253*2 c000 2000 0 253*2 c000 2000 0 253*2 c000 2000 0 253*2 c000 2000 0 253*2 c000 2000 0 253*2 c000
  //   2000 0 253*2 c000 2000 0 253*2 c000 2000 0 253*2 c000 2000 0 253*2 c000 2000 0 253*2 c000 2000 0
  //   253*2 c000 2000 0 253*2 c000 2000 0 253*2 c000 2000 0 253*2 c000 2000 0 253*2 c000 2000 0 253*2 c000
  //   2000 0 253*2 c000 2000 0 253*2 c000 2000 0 253*2 c000 2000 0 253*2 c000 2000 0 253*2 c000 2000 0
  //   253*2 c000 2000 0 253*2 c000 2000 0 253*2 c000 2000 0 253*2 c000 2000 0 253*2 c000 2000 0 253*2 c000
  //   2000 0 253*2 c000 2000 0 253*2 c000 2000 0 253*2 c000 2000 0 253*2 c000 2000 0 253*2 c000 2000 0
  //   253*2 c000 2000 0 253*2 c000 2000 0 253*2 c000 2000 0 253*2 c000 2000 0 253*2 c000 2000 0 253*2 c000
  //   2000 0 253*2 c000 2000 0 253*2 c000 2000 0 253*2 c000 2000 0 253*2 c000 2000 0 253*2 c000 2000 0
  //   253*2 c000 2000 0 253*2 c000 2000 0 253*2 c000 2000 0 253*2 c000 2000 0 253*2 c000 2000 0 253*2 c000
  //   2000 0 253*2 c000 2000 0 253*2 c000 2000 0 253*2 c000 2000 0 253*2 c000 2000 0 253*2 c000 2000 0
  //   253*2 c000 2000 0 253*2 c000 2000 0 253*2 c000 2000 0 253*2 c000 2000 0 253*2 c000 2000 0 253*2 c000
  //   2000 0 253*2 c000 2000 0 253*2 c000 2000 0 253*2 c000 2000 0 253*2 c000 2000 0 253*2 c000 2000 0
  //   253*2 c000 2000 0 253*2 c000 2000 0 253*2 c000 2000 0 253*2 c000 2000 0 253*2 c000 2000 0 253*2 c000
  //   2000 0 253*2 c000 2000 0 253*2 c000 2000 0 253*2 c000 2000 0 253*2 c000 2000 0 253*2 c000 2000 0
  //   253*2 c000 2000 0 253*2 c000 2000 0 253*2 c000 2000 0 253*2 c000 2000 0 253*2 c000 2000 0 253*2 c000
  //   2000 0 253*2 c000 2000 0 253*2 c000 2000 0 253*2 c000 2000 0 253*2 c000 2000 0 253*2 c000 2000 0
  //   253*2 c000 2000 0 253*2 c000 2000 0 253*2 c000 2000 0 253*2 c000 2000 0 253*2 c000 2000 0 253*2 c000
  //   2000 0 253*2 c000 2000 0 253*2 c000 2000 0 253*2 c000 2000 0 253*2 c000 2000 0 253*2 c000 2000 0
  //   253*2 c000 2000 0 253*2 c000 2000 0 253*2 c000 2000 0 253*2 c000 2000 0 253*2 c000 2000 0 253*2 c000
  //   2000 0 253*2 c000 2000 0 253*2 c000 2000 0 253*2 c000 2000 0 253*2 c000 2000 0 253*2 c000 2000 0
  //   253*2 c000 2000 0 253*2 c000 2000 0 253*2 c000 2000 0 253*2 c000 2000 0 253*2 c000 2000 0 253*2 c000
  //   2000 0 253*2 c000 2000 0 253*2 c000 2000 0 253*2 c000 2000 0 253*2 c000 2000 0 253*2 c000 2000 0
  //   253*2 c000 2000 0 253*2 c000 2000 0 253*2 c000 2000 0 253*2 c000 2000 0 253*2 c000 2000 0 253*2 c000
  //   2000 0 253*2 c000 2000 0 253*2 c000 2000 0 253*2 c000 2000 0 253*2 c000 2000 0 253*2 c000 2000 0
  //   253*2 c000 2000 0 253*2 c000 2000 0 253*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
endmodule
